# Fritzing sketch weather (saved by Fritzing 0.9.4)
circuit board: 6cm x 4cm
breadboards: 1

parts:
  Gizwits_WiFi_Witty_ESP-12F1 = Gizwits WiFi Witty ESP-12F
  RHT1 = Humidity and Temperature Sensor RHT03
  C2 = Ceramic Capacitor [capacitance="100 nF" package="1206 [SMD, multilayer]"]
  U1 = Voltage Regulator - 3.3V [package="TO220 [THT]"]
  LiPo_4_2V = 4 x AAA Battery Mount
  C1 = Electrolytic Capacitor [capacitance=1000µF package="300 mil [THT, electrolytic]"]
  S1_RESET = Pushbutton [package="[THT]"]
  S2_MODE = Pushbutton [package="[THT]"]
  R1 = Resistor [tolerance=±5% resistance=10k package=THT]
  R2 = Resistor [tolerance=±5% resistance=10k package=THT]
  R3 = Resistor [tolerance=±5% resistance=220k package=THT]
  R4 = Resistor [tolerance=±5% resistance=68k package=THT]

nets:
  N1: Gizwits_WiFi_Witty_ESP-12F1.REST, Gizwits_WiFi_Witty_ESP-12F1.GPIO0, S1_RESET.Pin_3, S1_RESET.Pin_4, R2.Pin_1
  N2: Gizwits_WiFi_Witty_ESP-12F1.ADC, R3.Pin_1, R4.Pin_0
  VCC: Gizwits_WiFi_Witty_ESP-12F1.CH_PD, Gizwits_WiFi_Witty_ESP-12F1.VCC, RHT1.Vcc, C2.1, U1.output_voltage, C1.+, S2_MODE.Pin_3, S2_MODE.Pin_4, R2.Pin_0
  N3: Gizwits_WiFi_Witty_ESP-12F1.GPIO14, S2_MODE.Pin_1, R1.Pin_0
  GND: Gizwits_WiFi_Witty_ESP-12F1.GND, RHT1.GND_2, C2.0, U1.GND, LiPo_4_2V.-, C1.-, S1_RESET.Pin_1, S1_RESET.Pin_2, R1.Pin_1, R4.Pin_1
  N4: Gizwits_WiFi_Witty_ESP-12F1.GPIO4, RHT1.Data-signal
  N5: U1.input_voltage, LiPo_4_2V.+, R3.Pin_0
